// Logisim project reptile.circ as structural Verilog: 6 circuits, main circuit main
// Register Bank
module RegisterBank (
  input  [15:0] DOUT1,
  input  [15:0] DOUT2,
  input  [15:0] DOUT3,
  input  [15:0] DOUT4,
  input  [2:0] Reg_Select,
  input  [15:0] DOUT5,
  input  [15:0] DOUT6,
  input  REG_LOAD,
  input  [15:0] DOUT7,
  input  [15:0] DOUT8,
  input  [15:0] DATA_IN,
  input  Clock
);

  wire and_1_out, and_2_out, and_3_out, and_4_out, and_5_out, and_6_out, and_7_out, and_8_out,
       decoder_1_out0, decoder_1_out1, decoder_1_out2, decoder_1_out3, decoder_1_out4, decoder_1_out5,
       decoder_1_out6, decoder_1_out7;
  wire [2:0] undriven;
  wire [15:0] register_1_q, register_2_q, register_3_q, register_4_q, register_5_q, register_6_q,
       register_7_q, register_8_q;

  Decoder #(.select(3), .enable("false")) decoder_1 (
    .out0(decoder_1_out0), .out1(decoder_1_out1), .out2(decoder_1_out2), .out3(decoder_1_out3),
    .out4(decoder_1_out4), .out5(decoder_1_out5), .out6(decoder_1_out6), .out7(decoder_1_out7), .sel(undriven));
  and and_1 (and_1_out, decoder_1_out0, REG_LOAD);
  and and_2 (and_2_out, decoder_1_out1, REG_LOAD);
  and and_3 (and_3_out, decoder_1_out2, REG_LOAD);
  and and_4 (and_4_out, decoder_1_out3, REG_LOAD);
  and and_5 (and_5_out, decoder_1_out4, REG_LOAD);
  and and_6 (and_6_out, decoder_1_out5, REG_LOAD);
  and and_7 (and_7_out, decoder_1_out6, REG_LOAD);
  and and_8 (and_8_out, decoder_1_out7, REG_LOAD);
  Register #(.width(16)) register_1 (.D(DATA_IN), .en(and_1_out), .Q(register_1_q), .clk(Clock));  // open: clr
  Register #(.width(16)) register_2 (.D(DATA_IN), .en(and_2_out), .Q(register_2_q), .clk(Clock));  // open: clr
  Register #(.width(16)) register_3 (.D(DATA_IN), .en(and_3_out), .Q(register_3_q), .clk(Clock));  // open: clr
  Register #(.width(16)) register_4 (.D(DATA_IN), .en(and_4_out), .Q(register_4_q), .clk(Clock));  // open: clr
  Register #(.width(16)) register_5 (.D(DATA_IN), .en(and_5_out), .Q(register_5_q), .clk(Clock));  // open: clr
  Register #(.width(16)) register_6 (.D(DATA_IN), .en(and_6_out), .Q(register_6_q), .clk(Clock));  // open: clr
  Register #(.width(16)) register_7 (.D(DATA_IN), .en(and_7_out), .Q(register_7_q), .clk(Clock));  // open: clr
  Register #(.width(16)) register_8 (.D(DATA_IN), .en(and_8_out), .Q(register_8_q), .clk(Clock));  // open: clr
endmodule

module main (
);

  wire alu_1_zf, ARMUX, Clock, IRLOAD, MEMLOAD, MUX, PCINC, PCLOAD, REGLOAD, undriven_8, undriven_9,
       undriven_10, undriven_11, undriven_12, undriven_13, undriven_14, undriven_15, undriven_16,
       undriven_17, undriven_18, undriven_19, undriven_20, undriven_21, undriven_22, undriven_23,
       undriven_24, undriven_25, undriven_26, undriven_27, undriven_28, undriven_29, undriven_30,
       undriven_31, undriven_32, undriven_33, undriven_34, undriven_35, ZF, ZFLOAD;
  wire [2:0] IR_q, IR_q_3;
  wire [3:0] ram_1_data_2;
  wire [8:3] IR_q_2;
  wire [11:0] ram_1_data;
  wire [15:0] alu_1_result, multiplexer_1_out, multiplexer_2_out, multiplexer_3_out, multiplexer_4_out,
       pc_1_pcout, res, undriven, undriven_2, undriven_3, undriven_4, undriven_5, undriven_6, undriven_7;

  Multiplexer #(.width(16), .enable("false")) multiplexer_1 (
    .in0(pc_1_pcout), .in1(multiplexer_4_out), .out(multiplexer_1_out), .sel(ARMUX));
  PC pc_1 (.PCIN({IR_q_3, IR_q_2, IR_q}), .PC_LOAD(PCLOAD), .PC_INC(PCINC), .clock(Clock), .PCOUT(pc_1_pcout));
  RAM #(.addrWidth(16), .dataWidth(16), .bus("separate")) ram_1 (
    .addr(multiplexer_1_out), .din(multiplexer_2_out), .data({ram_1_data_2, ram_1_data}), .str(MEMLOAD),
    .clk(Clock), .ld(1'b1));  // open: sel, clr
  RegisterBank registerbank_1 (
    .DOUT1(res), .DOUT2(undriven), .DOUT3(undriven_2), .DOUT4(undriven_3), .Reg_Select(IR_q),
    .DOUT5(undriven_4), .DOUT6(undriven_5), .REG_LOAD(REGLOAD), .DOUT7(undriven_6), .DOUT8(undriven_7),
    .DATA_IN(multiplexer_3_out), .Clock(Clock));
  Register #(.width(1)) register_1 (.D(alu_1_zf), .en(ZFLOAD), .Q(ZF), .clk(Clock));  // open: clr
  Multiplexer #(.select(3), .width(16), .enable("false")) multiplexer_2 (
    .in0(res), .in1(undriven), .in2(undriven_2), .in3(undriven_3), .in4(undriven_4), .in5(undriven_5),
    .in6(undriven_6), .in7(undriven_7), .out(multiplexer_2_out), .sel(IR_q_2[8:6]));
  Multiplexer #(.width(16), .enable("false")) multiplexer_3 (
    .in0(alu_1_result), .in1({ram_1_data_2, ram_1_data}), .out(multiplexer_3_out), .sel(MUX));
  ALU alu_1 (
    .RESULT(alu_1_result), .Din1(multiplexer_2_out), .Din2(multiplexer_4_out), .ZF(alu_1_zf),
    .alucode2(IR_q_2[8:6]), .alucode(IR_q_3));
  Multiplexer #(.select(3), .width(16), .enable("false")) multiplexer_4 (
    .in0(res), .in1(undriven), .in2(undriven_2), .in3(undriven_3), .in4(undriven_4), .in5(undriven_5),
    .in6(undriven_6), .in7(undriven_7), .out(multiplexer_4_out), .sel(IR_q_2[5:3]));
  Clock clock_1 (.out(Clock));
  Register #(.width(12)) IR (.D(ram_1_data), .en(IRLOAD), .Q({IR_q_3, IR_q_2, IR_q}), .clk(Clock));  // open: clr
  ControlUnit controlunit_1 (
    .ZF(ZF), .Opcode(ram_1_data_2), .IRLOAD(IRLOAD), .MEMLOAD(MEMLOAD), .MUX(MUX), .ZFLOAD(ZFLOAD),
    .REGLOAD(REGLOAD), .ARMUX(ARMUX), .PCINC(PCINC), .PCLOAD(PCLOAD), .Clock(Clock));
  _7segment u_7segment_1 (
    .D(res[15]), .C(res[14]), .B(res[13]), .A(res[12]), .A_2(undriven_12), .B_2(undriven_14),
    .c_2(undriven_11), .d_2(undriven_13), .e(undriven_9), .f(undriven_10), .g(undriven_8));
  _7_Segment_Display u_7_segment_display_1 (
    .g(undriven_8), .f(undriven_10), .a(undriven_12), .b(undriven_14), .e(undriven_9), .d(undriven_11),
    .c(undriven_13));  // open: dp
  _7segment u_7segment_2 (
    .D(res[11]), .C(res[10]), .B(res[9]), .A(res[8]), .A_2(undriven_19), .B_2(undriven_21),
    .c_2(undriven_18), .d_2(undriven_20), .e(undriven_16), .f(undriven_17), .g(undriven_15));
  _7_Segment_Display u_7_segment_display_2 (
    .g(undriven_15), .f(undriven_17), .a(undriven_19), .b(undriven_21), .e(undriven_16), .d(undriven_18),
    .c(undriven_20));  // open: dp
  _7segment u_7segment_3 (
    .D(res[7]), .C(res[6]), .B(res[5]), .A(res[4]), .A_2(undriven_26), .B_2(undriven_28), .c_2(undriven_25),
    .d_2(undriven_27), .e(undriven_23), .f(undriven_24), .g(undriven_22));
  _7_Segment_Display u_7_segment_display_3 (
    .g(undriven_29), .f(undriven_31), .a(undriven_33), .b(undriven_35), .e(undriven_30), .d(undriven_32),
    .c(undriven_34));  // open: dp
  _7_Segment_Display u_7_segment_display_4 (
    .g(undriven_22), .f(undriven_24), .a(undriven_26), .b(undriven_28), .e(undriven_23), .d(undriven_25),
    .c(undriven_27));  // open: dp
  _7segment u_7segment_4 (
    .D(res[3]), .C(res[2]), .B(res[1]), .A(res[0]), .A_2(undriven_33), .B_2(undriven_35), .c_2(undriven_32),
    .d_2(undriven_34), .e(undriven_30), .f(undriven_31), .g(undriven_29));
endmodule

module ALU (
  input  [15:0] Din1,
  input  [15:0] Din2,
  input  [2:0] alucode,
  input  [2:0] alucode2,
  output [15:0] RESULT,
  output ZF
);

  wire [15:0] adder_1_out, adder_2_out, and_1_out, multiplexer_1_out, not_1_out, or_1_out, subtractor_1_out,
       subtractor_2_out, xor_1_out;

  Adder #(.width(16)) adder_1 (.a(Din1), .b(Din2), .out(adder_1_out));  // open: cin, cout
  Subtractor #(.width(16)) subtractor_1 (.a(Din1), .b(Din2), .out(subtractor_1_out));  // open: bin, bout
  assign and_1_out = Din1 & Din2;  // AND_Gate and_1, 16 bits wide
  assign or_1_out = Din1 | Din2;  // OR_Gate or_1, 16 bits wide
  assign xor_1_out = Din1 ^ Din2;  // XOR_Gate xor_1, 16 bits wide
  assign not_1_out = ~Din2;  // NOT_Gate not_1, 16 bits wide
  Adder #(.width(16)) adder_2 (.a(Din2), .b(16'h1), .out(adder_2_out));  // open: cin, cout
  Subtractor #(.width(16)) subtractor_2 (.a(Din2), .b(16'h1), .out(subtractor_2_out));  // open: bin, bout
  Multiplexer #(.select(3), .width(16), .enable("false")) multiplexer_1 (
    .in0(not_1_out), .in1(Din2), .in2(adder_2_out), .in3(subtractor_2_out), .in4({16{1'b0}}),
    .in5({16{1'b0}}), .in6({16{1'b0}}), .in7({16{1'b0}}), .out(multiplexer_1_out), .sel(alucode2));
  Multiplexer #(.select(3), .width(16), .enable("false")) multiplexer_2 (
    .in0(adder_1_out), .in1(subtractor_1_out), .in2(and_1_out), .in3(or_1_out), .in4(xor_1_out),
    .in5(multiplexer_1_out), .in6({16{1'b0}}), .in7({16{1'b0}}), .out(RESULT), .sel(alucode));
  nor nor_1 (ZF, RESULT[0], RESULT[1], RESULT[2], RESULT[3], RESULT[4], RESULT[5], RESULT[6], RESULT[7], RESULT[9], RESULT[10], RESULT[11], RESULT[12], RESULT[13], RESULT[14], RESULT[15], RESULT[8]);
endmodule

module _7segment (
  input  D,
  input  C,
  input  B,
  input  A,
  input  A_2,
  input  B_2,
  input  c_2,
  input  d_2,
  input  e,
  input  f,
  input  g
);

  wire and_1_out, and_2_out, and_3_out, and_4_out, and_5_out, and_6_out, and_7_out, and_8_out, and_9_out,
       and_10_out, and_11_out, and_12_out, and_13_out, and_14_out, and_15_out, and_16_out, and_17_out,
       and_18_out, and_19_out, and_20_out, and_21_out, and_22_out, and_23_out, and_24_out, and_25_out,
       and_26_out, and_27_out, and_28_out, and_29_out, and_30_out, and_31_out, and_32_out, and_33_out,
       and_34_out, and_35_out, and_36_out, and_37_out, and_38_out, and_39_out, and_40_out, and_41_out,
       and_42_out, and_43_out, and_44_out, and_45_out, and_46_out, not_1_out, not_2_out, not_3_out,
       not_4_out, not_5_out, not_6_out, not_7_out, not_8_out, not_9_out, not_10_out, not_11_out, not_12_out,
       not_13_out, not_14_out, not_15_out, not_16_out, not_17_out, not_18_out, not_19_out, not_20_out,
       not_21_out, not_22_out, not_23_out, not_24_out, not_25_out, not_26_out, not_27_out, not_28_out,
       not_29_out, not_30_out, not_31_out, not_32_out, not_33_out, not_34_out, not_35_out, not_36_out,
       not_37_out, not_38_out, not_39_out, not_40_out, not_41_out, not_42_out, not_43_out, or_1_out,
       or_2_out, or_3_out, or_4_out, or_5_out, or_6_out, or_7_out, or_8_out, or_9_out, or_10_out, or_11_out,
       or_12_out, or_13_out, or_14_out, or_15_out, or_16_out, or_17_out, or_18_out, or_19_out, or_20_out,
       or_21_out;

  not not_1 (not_1_out, C);
  not not_2 (not_2_out, D);
  not not_3 (not_3_out, B);
  not not_4 (not_4_out, D);
  not not_5 (not_5_out, B);
  not not_6 (not_6_out, D);
  not not_7 (not_7_out, B);
  not not_8 (not_8_out, D);
  not not_9 (not_9_out, B);
  not not_10 (not_10_out, D);
  not not_11 (not_11_out, C);
  not not_12 (not_12_out, C);
  not not_13 (not_13_out, B);
  not not_14 (not_14_out, B);
  not not_15 (not_15_out, A);
  not not_16 (not_16_out, D);
  and and_1 (and_1_out, not_16_out, C);
  not not_17 (not_17_out, B);
  not not_18 (not_18_out, C);
  not not_19 (not_19_out, A);
  not not_20 (not_20_out, D);
  not not_21 (not_21_out, C);
  not not_22 (not_22_out, A);
  not not_23 (not_23_out, D);
  not not_24 (not_24_out, D);
  and and_2 (and_2_out, D, not_1_out);
  not not_25 (not_25_out, B);
  not not_26 (not_26_out, D);
  not not_27 (not_27_out, C);
  and and_3 (and_3_out, not_2_out, not_3_out);
  not not_28 (not_28_out, A);
  and and_4 (and_4_out, not_6_out, not_7_out);
  and and_5 (and_5_out, not_8_out, A);
  not not_29 (not_29_out, D);
  not not_30 (not_30_out, C);
  not not_31 (not_31_out, A);
  and and_6 (and_6_out, not_12_out, B);
  not not_32 (not_32_out, C);
  not not_33 (not_33_out, A);
  not not_34 (not_34_out, A);
  not not_35 (not_35_out, A);
  not not_36 (not_36_out, C);
  not not_37 (not_37_out, A);
  and and_7 (and_7_out, not_26_out, not_27_out);
  and and_8 (and_8_out, and_3_out, not_28_out);
  not not_38 (not_38_out, C);
  not not_39 (not_39_out, A);
  and and_9 (and_9_out, not_4_out, B);
  and and_10 (and_10_out, D, not_5_out);
  or or_1 (or_1_out, and_4_out, and_5_out);
  and and_11 (and_11_out, not_9_out, A);
  and and_12 (and_12_out, not_29_out, C);
  and and_13 (and_13_out, D, not_30_out);
  and and_14 (and_14_out, not_10_out, not_11_out);
  and and_15 (and_15_out, and_14_out, not_31_out);
  and and_16 (and_16_out, and_6_out, A);
  and and_17 (and_17_out, C, not_13_out);
  and and_18 (and_18_out, C, B);
  not not_40 (not_40_out, A);
  not not_41 (not_41_out, B);
  and and_19 (and_19_out, not_32_out, not_33_out);
  and and_20 (and_20_out, B, not_34_out);
  and and_21 (and_21_out, D, B);
  and and_22 (and_22_out, D, C);
  and and_23 (and_23_out, not_14_out, not_15_out);
  and and_24 (and_24_out, and_1_out, not_17_out);
  and and_25 (and_25_out, not_18_out, B);
  and and_26 (and_26_out, B, not_19_out);
  and and_27 (and_27_out, not_20_out, C);
  not not_42 (not_42_out, B);
  not not_43 (not_43_out, C);
  and and_28 (and_28_out, not_21_out, not_22_out);
  and and_29 (and_29_out, not_23_out, B);
  and and_30 (and_30_out, not_24_out, C);
  and and_31 (and_31_out, C, B);
  and and_32 (and_32_out, and_2_out, not_25_out);
  or or_2 (or_2_out, and_7_out, and_8_out);
  and and_33 (and_33_out, not_38_out, not_39_out);
  and and_34 (and_34_out, and_9_out, A);
  and and_35 (and_35_out, and_10_out, A);
  or or_3 (or_3_out, or_1_out, and_11_out);
  or or_4 (or_4_out, and_12_out, and_13_out);
  or or_5 (or_5_out, and_15_out, and_16_out);
  and and_36 (and_36_out, and_17_out, A);
  and and_37 (and_37_out, and_18_out, not_40_out);
  and and_38 (and_38_out, D, not_41_out);
  or or_6 (or_6_out, and_23_out, and_24_out);
  and and_39 (and_39_out, C, not_35_out);
  and and_40 (and_40_out, D, not_36_out);
  and and_41 (and_41_out, D, B);
  or or_7 (or_7_out, and_25_out, and_26_out);
  and and_42 (and_42_out, and_27_out, not_42_out);
  and and_43 (and_43_out, D, not_43_out);
  and and_44 (and_44_out, D, A);
  or or_8 (or_8_out, and_28_out, and_29_out);
  and and_45 (and_45_out, and_30_out, A);
  or or_9 (or_9_out, and_31_out, and_32_out);
  and and_46 (and_46_out, D, not_37_out);
  or or_10 (or_10_out, or_2_out, and_33_out);
  or or_11 (or_11_out, and_34_out, and_35_out);
  or or_12 (or_12_out, or_5_out, and_36_out);
  or or_13 (or_13_out, and_37_out, and_38_out);
  or or_14 (or_14_out, and_19_out, and_20_out);
  or or_15 (or_15_out, and_21_out, and_22_out);
  or or_16 (or_16_out, or_6_out, and_39_out);
  or or_17 (or_17_out, and_40_out, and_41_out);
  or or_18 (or_18_out, or_7_out, and_42_out);
  or or_19 (or_19_out, and_43_out, and_44_out);
  or or_20 (or_20_out, or_8_out, and_45_out);
  or or_21 (or_21_out, or_9_out, and_46_out);
  or or_22 (B_2, or_10_out, or_11_out);
  or or_23 (c_2, or_3_out, or_4_out);
  or or_24 (d_2, or_12_out, or_13_out);
  or or_25 (e, or_14_out, or_15_out);
  or or_26 (f, or_16_out, or_17_out);
  or or_27 (g, or_18_out, or_19_out);
  or or_28 (A_2, or_20_out, or_21_out);
endmodule

// Control Unit
module ControlUnit (
  input  [3:0] Opcode,
  input  ZF,
  input  Clock,
  output MEMLOAD,
  output IRLOAD,
  output MUX,
  output ZFLOAD,
  output REGLOAD,
  output ARMUX,
  output PCINC,
  output PCLOAD
);

  wire not_1_out, not_2_out, not_3_out;
  wire [1:1] and_1_out;
  wire [3:0] multiplexer_1_out, multiplexer_2_out, register_1_q;
  wire [8:8] rom_1_data;

  not not_1 (not_1_out, Opcode[1]);
  not not_2 (not_2_out, Opcode[0]);
  and and_1 (and_1_out[1], not_2_out, not_1_out, Opcode[2], not_3_out);
  not not_3 (not_3_out, Opcode[3]);
  Multiplexer #(.select(2), .width(4), .enable("false")) multiplexer_1 (
    .in0(Opcode), .in1(Opcode), .in2(4'b0000), .in3(4'b0101), .out(multiplexer_1_out),
    .sel({and_1_out[1], ZF}));
  Multiplexer #(.width(4), .enable("false")) multiplexer_2 (
    .in0(4'b0000), .in1(multiplexer_1_out), .out(multiplexer_2_out), .sel(rom_1_data[8]));
  Register #(.width(4)) register_1 (.D(multiplexer_2_out), .en(1'b1), .Q(register_1_q), .clk(Clock));  // open: clr
  ROM #(.addrWidth(4), .dataWidth(9)) rom_1 (
    .addr(register_1_q), .data({rom_1_data[8], PCLOAD, PCINC, ARMUX, REGLOAD, ZFLOAD, MUX, MEMLOAD, IRLOAD}));  // open: sel

  // Notes on the sheet:
  //   contents of rom_1 (hex, n*v repeats v):
  //   141 54 34 22 0 80 0 18
endmodule

module PC (
  input  [11:0] PCIN,
  input  clock,
  input  PC_INC,
  input  PC_LOAD,
  output [15:0] PCOUT
);

  wire or_1_out;
  wire [15:0] adder_1_out, adder_2_out, bit_extender_1_out, multiplexer_1_out, multiplexer_2_out;

  assign bit_extender_1_out = {{4{1'b0}}, PCIN};  // Bit_Extender bit_extender_1
  Adder #(.width(16)) adder_1 (.a(PCOUT), .b(16'h1), .out(adder_1_out));  // open: cin, cout
  Adder #(.width(16)) adder_2 (.a(bit_extender_1_out), .b(PCOUT), .out(adder_2_out));  // open: cin, cout
  Multiplexer #(.width(16), .enable("false")) multiplexer_1 (
    .in0(PCOUT), .in1(adder_2_out), .out(multiplexer_1_out), .sel(PC_LOAD));
  Multiplexer #(.width(16), .enable("false")) multiplexer_2 (
    .in0(multiplexer_1_out), .in1(adder_1_out), .out(multiplexer_2_out), .sel(PC_INC));
  or or_1 (or_1_out, PC_LOAD, PC_INC);
  Register #(.width(16)) register_1 (.D(multiplexer_2_out), .en(or_1_out), .Q(PCOUT), .clk(clock));  // open: clr

  // Other names for the same wires on the sheet: currPC[15:0] = PCOUT
endmodule
